# Fritzing sketch NaniteSMD (saved by Fritzing 0.9.2b)
circuit board: 8.46667cm x 5.64444cm
breadboards: 1

parts:
  68 = Resistor [tolerance=±0.05% resistance=68 package=THT]
  68_2 = Resistor [tolerance=±0.05% resistance=68 package=THT]
  3_6v = DIODE-ZENER [package=diode-zener]
  3_6v_2 = DIODE-ZENER [package=diode-zener]
  USB_MiniB = USB Connectors [package=usb-minib-nostop]
  part = Resistor [tolerance=±5% resistance=10k package=THT]
  U1 = ATTINY13 [package=so]

nets:
  N1: 68.Pin_0, 3_6v_2.C, USB_MiniB.D+
  N2: 68.Pin_1, U1.PB4(ADC2)
  N3: 68_2.Pin_0, 3_6v.C, USB_MiniB.D-, part.Pin_0
  N4: 68_2.Pin_1, U1.PB3(ADC3)
  GND: 3_6v.A, 3_6v_2.A, USB_MiniB.GND, U1.GND
  5V: USB_MiniB.VBUS, part.Pin_1, U1.VCC
